# Fritzing sketch CarWiring (saved by Fritzing 0.9.3b)

parts:
  Part1 = Arduino MKR1000
  3-pins_Hall_Effect_Sensor1 = mystery part, 3 pins [chip_label="Hall Effect Sensor"]
  R1 = Resistor [tolerance=±5% resistance=10k package="0603 [SMD]"]
  R2 = Resistor [tolerance=±5% resistance=1k package="0603 [SMD]"]
  R3 = Resistor [tolerance=±5% resistance=2k package="0603 [SMD]"]
  LED1 = smd LED [color="Red (633nm)" package="0603 [SMD]"]
  LED2 = smd LED [color="Red (633nm)" package="0603 [SMD]"]
  R4 = Resistor [tolerance=±5% resistance=330 package="2512 [SMD]"]
  Part2 = Arduino MKR1000
  3-pins_Hall_Effect_Sensor2 = mystery part, 3 pins [chip_label="Hall Effect Sensor"]
  R5 = Resistor [tolerance=±5% resistance=10k package="0603 [SMD]"]

nets:
  N1: Part1.D0, R4.Pin_0
  N2: Part1.D6, R2.Pin_0, R3.Pin_0
  N3: Part1.GND, 3-pins_Hall_Effect_Sensor1.pin2, R3.Pin_1, LED1.cathode, LED2.cathode
  N4: Part1.5V, 3-pins_Hall_Effect_Sensor1.pin1, R1.Pin_1
  N5: 3-pins_Hall_Effect_Sensor1.pin3, R1.Pin_0, R2.Pin_1
  N6: LED1.anode, LED2.anode, R4.Pin_1
  N7: Part2.D6, 3-pins_Hall_Effect_Sensor2.pin3, R5.Pin_0
  N8: Part2.GND, 3-pins_Hall_Effect_Sensor2.pin2
  N9: Part2.VCC, R5.Pin_1
  N10: Part2.5V, 3-pins_Hall_Effect_Sensor2.pin1

custom parts:
  Arduino MKR1000: MKR1000 is a powerful board that combines the functionality of the Zero and the Wi-Fi Shield. It is the ideal solution for makers wanting to design IoT projects with minimal previous experience in networking
