# Fritzing sketch BackendWiring (saved by Fritzing 0.9.3b)

parts:
  J3 = Basic Servo
  J5 = Basic Servo
  J6 = Basic Servo
  Raspberry_Pi_1 = Raspberry Pi 3 [part_number=RPI-3-V1.2]
  J7 = Basic Servo
  U1 = WS2812 RGB LED strip
  VCC1 = Battery
  C1 = Electrolytic Capacitor [capacitance=100µF package="200 mil [THT, electrolytic]"]

nets:
  GND: J3.gnd, J5.gnd, J6.gnd, Raspberry_Pi_1.GND, J7.gnd, U1.GND, VCC1.-, C1.-
  VCC: J3.vcc, J5.vcc, Raspberry_Pi_1.5V, J7.vcc, C1.+
  N1: J3.pulse, Raspberry_Pi_1.GIPO6
  N2: J5.pulse, Raspberry_Pi_1.GIPO19
  VCC_2: J6.vcc, U1.VCC, VCC1.+
  N3: J6.pulse, Raspberry_Pi_1.GIPO13
  N4: Raspberry_Pi_1.GIPO5, J7.pulse
  N5: Raspberry_Pi_1.GIPO18, U1.DIN

custom parts:
  WS2812 RGB LED strip: WS2812 strip
