# Fritzing sketch BackendWiring (saved by Fritzing 0.9.3b)
breadboards: 1

parts:
  J3 = Basic Servo
  J4 = Basic Servo
  J5 = Basic Servo
  J6 = Basic Servo
  Raspberry_Pi_1 = Raspberry Pi 3 [part_number=RPI-3-V1.2]
  J7 = Basic Servo
  J8 = Basic Servo
  U1 = WS2812 RGB LED strip
  VCC1 = Battery
  C1 = Electrolytic Capacitor [capacitance=100µF package="200 mil [THT, electrolytic]"]

nets:
  GND: J3.gnd, J4.gnd, J5.gnd, J6.gnd, Raspberry_Pi_1.GND, J7.gnd, J8.gnd, U1.GND, VCC1.-, C1.-
  VCC: J3.vcc, J4.vcc, J5.vcc, J6.vcc, Raspberry_Pi_1.5V, J7.vcc, J8.vcc
  N1: J3.pulse, Raspberry_Pi_1.GIPO17
  N2: J4.pulse, Raspberry_Pi_1.GIPO5
  N3: J5.pulse, Raspberry_Pi_1.GIPO22
  N4: J6.pulse, Raspberry_Pi_1.GIPO27
  N5: Raspberry_Pi_1.GIPO4, J7.pulse
  N6: Raspberry_Pi_1.GIPO6, J8.pulse
  N7: Raspberry_Pi_1.GIPO19, U1.DIN
  N8: U1.VCC, VCC1.+, C1.+

custom parts:
  WS2812 RGB LED strip: WS2812 strip
